# Fritzing sketch OpenVRT (saved by Fritzing 0.9.3b)
breadboards: 1

parts:
  Part1 = Arduino Mega 2560 (Rev3)
  Part2 = Arduino Motor Shield (Rev3)
  M1 = DC Motor
  Part3 = Bluetooth HC-05 Macho
  U1 = POT [package=pot_alpha_rv16af-20]
  R1 = Resistor [tolerance=±5% resistance=220 package="2512 [SMD]"]
  R2 = Resistor [tolerance=±5% resistance=470 package="2512 [SMD]"]
  R3 = Resistor [tolerance=±5% resistance=1k package=THT]
  M2 = fc-51 [package=THT]
  J1 = ATX24 Pin Power Supply Connector [package=atx24_right_angle]
  D1 = LTE-302 [package=lte-302]  # not connected
  R4 = Resistor [tolerance=±5% resistance=6.8k package="2512 [SMD]"]
  R5 = Resistor [tolerance=±5% resistance=220 package="2512 [SMD]"]

nets:
  N1: Part1.A8, U1.S
  N2: Part1.A0, Part2.A0
  N3: Part1.A1, Part2.A1
  N4: Part1.A2, Part2.A2
  N5: Part1.A3, Part2.A3
  N6: Part1.A4, Part2.A4
  N7: Part1.A5, Part2.A5
  N8: Part1.D21/SCL, Part1.SCL, Part2.SCL, R4.Pin_0, R5.Pin_0
  N9: Part1.D19/RX1, Part3.TXD
  N10: Part1.D18/TX1, R2.Pin_1
  N11: Part1.SDA, Part2.SDA
  N12: Part1.AREF, Part2.AREF
  GND: Part1.GND, Part2.GND, Part3.GND, U1.A, R3.Pin_1, M2.pin3, J1.12V
  N13: Part1.D13_PWM, Part2.D13/DirB
  N14: Part1.D12_PWM, Part2.D12/DirA
  N15: Part1.D11_PWM, Part2.D11_PWM/B
  N16: Part1.D10_PWM, Part2.D10_PWM
  N17: Part1.D9_PWM, Part2.D9/BreakeA
  N18: Part1.D8_PWM, Part2.D8/BreakeB
  N19: Part1.IOREF, Part2.IOREF#147
  N20: Part1.RESET, Part2.RESET
  3V3: Part1.3V3, Part2.3V3
  5V: Part1.5V, Part2.5V, Part3.VCC, U1.E, R1.Pin_0
  VIN: Part1.VIN, Part2.VIN
  N21: Part1.D0_RX0, Part2.IOREF#118
  N22: Part1.D1_TX0, Part2.D1/TX
  N23: Part1.D2_PWM, Part2.D2
  N24: Part1.D3_PWM, Part2.D3_PWM/A
  N25: Part1.D4_PWM, Part2.D4
  N26: Part1.D5_PWM, Part2.D5_PWM
  N27: Part1.D6_PWM, Part2.D6_PWM
  N28: Part1.D7_PWM, Part2.D7
  N29: Part2.A-, M1.pin_2
  N30: Part2.A+, M1.pin_1
  N31: Part2.VMOT, J1.GND
  N32: Part3.RXD, R2.Pin_0, R3.Pin_0
  N33: M2.pin1, R4.Pin_1

notes:
  LJ12A3-4-Z/BY
  12V
